// Logisim project 1.5.circ as structural Verilog: 1 circuit, main circuit main
module main (
  input  x,
  input  y,
  input  z,
  input  x_2,
  input  y_2,
  input  z_2,
  output F_x_y_z,
  output F_x_y_z_2
);

  wire and_1_out, and_2_out, and_3_out, nx_2_out, nx_out, ny_2_out, ny_out, nz_2_out, nz_out, or_2_out,
       or_3_out, or_4_out, or_5_out;

  not nx (nx_out, x);
  not ny (ny_out, y);
  not nz (nz_out, z);
  not nx_2 (nx_2_out, x_2);
  not ny_2 (ny_2_out, y_2);
  not nz_2 (nz_2_out, z_2);
  and and_1 (and_1_out, y, z);
  and and_2 (and_2_out, nx_2_out, y_2, z_2);
  and and_3 (and_3_out, nx_out, and_1_out);
  or or_1 (F_x_y_z_2, nx_2_out, x_2, and_2_out, nz_2_out, ny_2_out, nz_2_out);
  or or_2 (or_2_out, and_3_out, nz_out);
  or or_3 (or_3_out, or_2_out, ny_out);
  or or_4 (or_4_out, nx_out, or_3_out);
  or or_5 (or_5_out, or_4_out, nz_out);
  or or_6 (F_x_y_z, x, or_5_out);

  // Notes on the sheet:
  //   F(x;y;z)=1
  //   F(x;y;z)=1
  //   F(x;y;z)=!z+z*y*!x+!y+!x+!z+x
  //   F(x;y;z)=!z+z*y*!x+!y+!x+!z+x
endmodule
