// Logisim project 1.circ as structural Verilog: 1 circuit, main circuit main
module main (
  input  x,
  input  y,
  input  z,
  output F_x_y_z
);

  wire and_1_out, and_2_out, nx_out, ny_out, nz_out, or_1_out, or_2_out, or_3_out, or_4_out;

  not nx (nx_out, x);
  not ny (ny_out, y);
  not nz (nz_out, z);
  and and_1 (and_1_out, x, y);
  and and_2 (and_2_out, and_1_out, z);
  or or_1 (or_1_out, nx_out, and_2_out);
  or or_2 (or_2_out, or_1_out, nz_out);
  or or_3 (or_3_out, or_2_out, ny_out);
  or or_4 (or_4_out, or_3_out, z);
  or or_5 (F_x_y_z, x, or_4_out);

  // Notes on the sheet:
  //   F(x;y;z)=1
  //   F(x;y;z)= !x+x*y*z+!z+!y+z+x
endmodule
