// Logisim project 3.circ as structural Verilog: 1 circuit, main circuit main
module main (
  input  D2,
  input  D1,
  input  D0,
  input  C,
  input  E,
  output Q2,
  output nQ2,
  output Q1,
  output nQ1,
  output Q0,
  output nQ0
);

  wire and_1_out, and_2_out, and_3_out, and_4_out, and_5_out, and_6_out, nor_1_out, nor_3_out, nor_5_out,
       not_1_out, not_2_out, not_3_out;

  not not_1 (not_1_out, D2);
  not not_2 (not_2_out, D1);
  not not_3 (not_3_out, D0);
  and and_1 (and_1_out, not_1_out, C);
  and and_2 (and_2_out, C, D2);
  and and_3 (and_3_out, not_2_out, C);
  and and_4 (and_4_out, C, D1);
  and and_5 (and_5_out, not_3_out, C);
  and and_6 (and_6_out, C, D0);
  nor nor_1 (nor_1_out, and_1_out, nQ2);
  nor nor_2 (nQ2, nor_1_out, and_2_out);
  nor nor_3 (nor_3_out, and_3_out, nQ1);
  nor nor_4 (nQ1, nor_3_out, and_4_out);
  nor nor_5 (nor_5_out, and_5_out, nQ0);
  nor nor_6 (nQ0, nor_5_out, and_6_out);
  and and_7 (Q2, nor_1_out, E);
  and and_8 (Q1, nor_3_out, E);
  and and_9 (Q0, nor_5_out, E);
endmodule
