// Logisim project alu.circ as structural Verilog: 1 circuit, main circuit main
module main (
  input  p,
  input  INVa,
  input  a,
  input  ENa,
  input  b,
  input  ENb,
  input  A0,
  input  A1,
  output S,
  output P_2
);

  wire A_B_out, AB_out, and_1_out, and_2_out, and_3_out, and_4_out, and_5_out, and_6_out, and_7_out,
       and_8_out, and_9_out, and_10_out, and_11_out, and_12_out, nB_out, not_1_out, not_2_out, not_3_out,
       not_4_out, or_1_out, or_2_out, or_3_out;

  and and_1 (and_1_out, a, ENa);
  and and_2 (and_2_out, b, ENb);
  not not_1 (not_1_out, A0);
  not not_2 (not_2_out, A0);
  or or_1 (or_1_out, INVa, and_1_out);
  not not_3 (not_3_out, A1);
  not not_4 (not_4_out, A1);
  and and_3 (and_3_out, not_1_out, not_3_out);
  and and_4 (and_4_out, not_2_out, A1);
  and and_5 (and_5_out, A0, not_4_out);
  and and_6 (and_6_out, A1, A0);
  and AB (AB_out, or_1_out, and_2_out);
  or A_B (A_B_out, or_1_out, and_2_out);
  not nB (nB_out, and_2_out);
  and and_7 (and_7_out, AB_out, and_3_out);
  and and_8 (and_8_out, A_B_out, and_4_out);
  and and_9 (and_9_out, nB_out, and_5_out);
  or or_2 (or_2_out, or_1_out, and_2_out);
  or or_3 (or_3_out, p, or_2_out);
  and and_10 (and_10_out, p, or_2_out, and_6_out);
  and and_11 (and_11_out, and_2_out, or_1_out, and_6_out);
  and and_12 (and_12_out, or_3_out, and_6_out);
  or or_4 (P_2, and_10_out, and_11_out);
  or or_5 (S, and_7_out, and_8_out, and_9_out, and_12_out);
endmodule
