// Logisim project bhfbh.circ as structural Verilog: 1 circuit, main circuit main
module main (
  input  A0,
  input  A1,
  input  D0,
  input  D1,
  input  D2,
  input  D3,
  input  E,
  output Y
);

  wire and_1_out, and_2_out, and_3_out, and_4_out, and_5_out, and_6_out, and_7_out, and_8_out, not_1_out,
       not_2_out, undriven;

  not not_1 (not_1_out, A0);
  not not_2 (not_2_out, undriven);
  and and_1 (and_1_out, not_1_out, not_2_out);
  // AND_Gate and_2 has open pins: out=and_2_out
  buf and_3 (and_3_out, A1);  // AND_Gate
  and and_4 (and_4_out, undriven, A0);
  and and_5 (and_5_out, and_1_out, D0, E);
  and and_6 (and_6_out, and_2_out, D1, E);
  and and_7 (and_7_out, and_3_out, D2, E);
  and and_8 (and_8_out, and_4_out, D3, E);
  or or_1 (Y, and_5_out, and_6_out, and_7_out, and_8_out);
endmodule
