// Logisim project multipleksor.circ as structural Verilog: 1 circuit, main circuit main
module main (
  input  A2,
  input  A1,
  input  A0,
  input  D7,
  input  D6,
  input  D5,
  input  D4,
  input  D3,
  input  D2,
  input  D1,
  input  D0,
  input  E,
  output Y
);

  wire and_1_out, and_2_out, and_3_out, and_4_out, and_5_out, and_6_out, and_7_out, and_8_out, and_9_out,
       and_10_out, and_11_out, and_12_out, and_13_out, and_14_out, and_15_out, and_16_out, not_1_out,
       not_2_out, not_3_out;

  not not_1 (not_1_out, A0);
  not not_2 (not_2_out, A0);
  not not_3 (not_3_out, A2);
  and and_1 (and_1_out, A2, A0, A0);
  and and_2 (and_2_out, A2, A0, not_1_out);
  and and_3 (and_3_out, A2, not_2_out, A0);
  and and_4 (and_4_out, A2, not_2_out, not_1_out);
  and and_5 (and_5_out, not_3_out, A0, A0);
  and and_6 (and_6_out, A0, not_3_out, not_1_out);
  and and_7 (and_7_out, A0, not_3_out, not_2_out);
  and and_8 (and_8_out, not_1_out, not_2_out, not_3_out);
  and and_9 (and_9_out, and_1_out, D7, E);
  and and_10 (and_10_out, and_2_out, D6, E);
  and and_11 (and_11_out, and_3_out, D5, E);
  and and_12 (and_12_out, and_4_out, D4, E);
  and and_13 (and_13_out, and_5_out, D3, E);
  and and_14 (and_14_out, and_6_out, D2, E);
  and and_15 (and_15_out, and_7_out, D1, E);
  and and_16 (and_16_out, and_8_out, D0, E);
  or or_1 (Y, and_9_out, and_10_out, and_11_out, and_12_out, and_13_out, and_14_out, and_15_out, and_16_out);

  assign A1 = A0;

  // Notes on the sheet:
  //   Мультиплексор
endmodule
