// Logisim project дешифратор.circ as structural Verilog: 1 circuit, main circuit main
module main (
  input  A2,
  input  A1,
  input  A0,
  input  E,
  output D7,
  output D6,
  output D5,
  output D4,
  output D3,
  output D2,
  output D1,
  output D0
);

  wire and_1_out, and_2_out, and_3_out, and_4_out, and_5_out, and_6_out, and_7_out, and_8_out, not_1_out,
       not_2_out, not_3_out;

  not not_1 (not_1_out, A2);
  not not_2 (not_2_out, A0);
  not not_3 (not_3_out, A1);
  and and_1 (and_1_out, A2, A1, A0);
  and and_2 (and_2_out, A2, A1, not_2_out);
  and and_3 (and_3_out, A2, not_3_out, A0);
  and and_4 (and_4_out, A2, not_3_out, not_2_out);
  and and_5 (and_5_out, not_1_out, A1, A0);
  and and_6 (and_6_out, A1, not_1_out, not_2_out);
  and and_7 (and_7_out, A0, not_1_out, not_3_out);
  and and_8 (and_8_out, not_2_out, not_3_out, not_1_out);
  and and_9 (D7, and_1_out, E);
  and and_10 (D6, and_2_out, E);
  and and_11 (D5, and_3_out, E);
  and and_12 (D4, and_4_out, E);
  and and_13 (D3, and_5_out, E);
  and and_14 (D2, and_6_out, E);
  and and_15 (D1, and_7_out, E);
  and and_16 (D0, and_8_out, E);

  // Notes on the sheet:
  //   Дешифратор
endmodule
