// Logisim project мультиплексор.circ as structural Verilog: 1 circuit, main circuit main
module main (
  input  A2,
  input  A1,
  input  A0,
  input  DO7,
  input  DO6,
  input  DO5,
  input  DO4,
  input  DO3,
  input  DO2,
  input  DO1,
  input  DO0,
  input  E,
  output Y
);

  wire and_1_out, and_2_out, and_3_out, and_4_out, and_5_out, and_6_out, and_7_out, and_8_out, and_9_out,
       and_10_out, and_11_out, and_12_out, and_13_out, and_14_out, and_15_out, and_16_out, not_1_out,
       not_2_out, not_3_out;

  not not_1 (not_1_out, A1);
  not not_2 (not_2_out, A2);
  not not_3 (not_3_out, A0);
  and and_1 (and_1_out, A2, A1, A0);
  and and_2 (and_2_out, A2, A1, not_3_out);
  and and_3 (and_3_out, A2, not_1_out, A0);
  and and_4 (and_4_out, A2, not_1_out, not_3_out);
  and and_5 (and_5_out, not_2_out, A1, A0);
  and and_6 (and_6_out, A1, not_2_out, not_3_out);
  and and_7 (and_7_out, A0, not_2_out, not_1_out);
  and and_8 (and_8_out, not_3_out, not_1_out, not_2_out);
  and and_9 (and_9_out, and_1_out, DO7, E);
  and and_10 (and_10_out, and_2_out, DO6, E);
  and and_11 (and_11_out, and_3_out, DO5, E);
  and and_12 (and_12_out, and_4_out, DO4, E);
  and and_13 (and_13_out, and_5_out, DO3, E);
  and and_14 (and_14_out, and_6_out, DO2, E);
  and and_15 (and_15_out, and_7_out, DO1, E);
  and and_16 (and_16_out, and_8_out, DO0, E);
  or or_1 (Y, and_9_out, and_10_out, and_11_out, and_12_out, and_13_out, and_14_out, and_15_out, and_16_out);
endmodule
