// Logisim project сумматоры.circ as structural Verilog: 1 circuit, main circuit main
module main (
  input  A,
  input  B,
  input  A_2,
  input  B_2,
  output P,
  output S,
  output S_2
);

  wire and_2_out, and_3_out, and_4_out, and_5_out, not_1_out, not_2_out, not_3_out, not_4_out;

  not not_1 (not_1_out, A);
  not not_2 (not_2_out, B);
  not not_3 (not_3_out, A_2);
  not not_4 (not_4_out, B_2);
  and and_1 (P, A, B);
  and and_2 (and_2_out, not_1_out, B);
  and and_3 (and_3_out, A, not_2_out);
  and and_4 (and_4_out, not_3_out, B_2);
  and and_5 (and_5_out, A_2, not_4_out);
  or or_1 (S, and_2_out, and_3_out);
  or or_2 (S_2, and_4_out, and_5_out);

  // Notes on the sheet:
  //   Полусумматор
  //   Четвертьсумматор
endmodule
